// Logisim project Guia_0501.circ as structural Verilog: 1 circuit, main circuit Guia_0501
module Guia_0501 (
  input  a,
  input  b,
  output s
);

  wire nor_1_out, nor_2_out, nor_3_out;

  nor nor_1 (nor_1_out, a, a);
  nor nor_2 (nor_2_out, b, b);
  nor nor_3 (nor_3_out, nor_2_out, nor_2_out);
  nor nor_4 (s, nor_1_out, nor_3_out);

  // Notes on the sheet:
  //   (a & ~b)    (NOR)
endmodule
