// Logisim project Guia_0503.circ as structural Verilog: 1 circuit, main circuit Guia_0503
module Guia_0503 (
  input  a,
  input  b,
  output s
);

  wire nor_1_out, nor_2_out;

  nor nor_1 (nor_1_out, a, a);
  nor nor_2 (nor_2_out, nor_1_out, b);
  nor nor_3 (s, nor_2_out, nor_2_out);

  // Notes on the sheet:
  //   (~a | b)    (NOR)
endmodule
