// Logisim project Guia_0504.circ as structural Verilog: 1 circuit, main circuit Guia_0504
module Guia_0504 (
  input  a,
  input  b,
  output s
);

  wire nand_1_out;

  nand nand_1 (nand_1_out, b, b);
  nand nand_2 (s, a, nand_1_out);

  // Notes on the sheet:
  //   ~(a & ~b)     (NAND)
endmodule
