// Logisim project Guia_0506.circ as structural Verilog: 1 circuit, main circuit Guia_0506
module Guia_0506 (
  input  a,
  input  b,
  output s
);

  wire nand_1_out, nand_2_out, nand_3_out, nand_4_out;

  nand nand_1 (nand_1_out, a, a);
  nand nand_2 (nand_2_out, b, b);
  nand nand_3 (nand_3_out, nand_1_out, b);
  nand nand_4 (nand_4_out, a, nand_2_out);
  nand nand_5 (s, nand_3_out, nand_4_out);

  // Notes on the sheet:
  //   ((a ^ b) = a xor b)     (NAND)
endmodule
