// Logisim project questao_01.circ as structural Verilog: 5 circuits, main circuit questao_1a
module questao_1a (
  input  x,
  input  y,
  input  z,
  output s
);

  wire and_1_out, and_2_out, not_1_out, not_2_out;

  not not_1 (not_1_out, x);
  not not_2 (not_2_out, y);
  and and_1 (and_1_out, x, z);
  and and_2 (and_2_out, not_1_out, not_2_out, z);
  or or_1 (s, and_1_out, and_2_out);
endmodule

module questao_1b (
  input  x,
  input  z,
  output s
);

  wire not_1_out;

  not not_1 (not_1_out, z);
  and and_1 (s, x, not_1_out);
endmodule

module questao_1c (
  input  x,
  input  y,
  output s
);

  wire not_1_out;

  not not_1 (not_1_out, x);
  or or_1 (s, not_1_out, y);
endmodule

module questao_1d (
  input  x,
  input  y,
  input  z,
  output s
);

  wire and_1_out, and_2_out, and_3_out, not_1_out, not_2_out, not_3_out, not_4_out;

  not not_1 (not_1_out, x);
  not not_2 (not_2_out, x);
  not not_3 (not_3_out, x);
  not not_4 (not_4_out, z);
  and and_1 (and_1_out, not_1_out, z);
  and and_2 (and_2_out, not_2_out, y);
  and and_3 (and_3_out, not_3_out, not_4_out);
  or or_1 (s, and_1_out, and_2_out, and_3_out);
endmodule

module questao_1e (
  input  x,
  input  y,
  input  z,
  output s
);

  wire and_1_out, not_1_out;

  and and_1 (and_1_out, x, y);
  not not_1 (not_1_out, z);
  or or_1 (s, and_1_out, not_1_out);
endmodule
