// Logisim project questao_02.circ as structural Verilog: 5 circuits, main circuit questao_2a
module questao_2a (
  input  x,
  input  z,
  output s
);

  wire not_1_out, not_2_out, or_1_out, or_2_out;

  not not_1 (not_1_out, x);
  not not_2 (not_2_out, z);
  or or_1 (or_1_out, x, z);
  or or_2 (or_2_out, not_1_out, not_2_out);
  and and_1 (s, or_1_out, or_2_out);
endmodule

module questao_2b (
  input  x,
  input  z,
  output s
);

  wire not_1_out, or_1_out, or_2_out;

  not not_1 (not_1_out, x);
  or or_1 (or_1_out, x, z);
  or or_2 (or_2_out, not_1_out, z);
  and and_1 (s, or_1_out, or_2_out);
endmodule

module questao_2c (
  input  x,
  input  z,
  input  y,
  output s
);

  wire and_1_out, and_2_out, not_1_out, not_2_out;

  not not_1 (not_1_out, z);
  not not_2 (not_2_out, x);
  and and_1 (and_1_out, x, not_1_out);
  and and_2 (and_2_out, not_2_out, y);
  or or_1 (s, and_1_out, and_2_out);
endmodule

module questao_2d (
  input  x,
  input  z,
  output s
);

  or or_1 (s, x, z);
endmodule

module questao_2e (
  input  X,
  input  Y,
  input  Z,
  output s
);

  wire and_1_out, and_2_out, and_3_out, not_1_out, not_2_out;

  not not_1 (not_1_out, Z);
  not not_2 (not_2_out, Y);
  and and_1 (and_1_out, X, not_1_out);
  and and_2 (and_2_out, X, Y);
  and and_3 (and_3_out, not_2_out, Z);
  or or_1 (s, and_1_out, and_2_out, and_3_out);
endmodule
