// Logisim project questao_03.circ as structural Verilog: 5 circuits, main circuit questao_3a
module questao_3a (
  input  w,
  input  z,
  input  x,
  input  y,
  output s
);

  wire and_1_out, and_2_out, and_3_out, not_1_out, not_2_out, not_3_out, not_4_out;

  not not_1 (not_1_out, w);
  and and_1 (and_1_out, not_1_out, z);
  not not_2 (not_2_out, y);
  and and_2 (and_2_out, x, not_2_out, w);
  not not_3 (not_3_out, y);
  not not_4 (not_4_out, w);
  and and_3 (and_3_out, not_3_out, not_4_out, z);
  or or_1 (s, and_1_out, and_2_out, and_3_out);
endmodule

module questao_3b (
  input  x,
  input  w,
  input  z,
  input  y,
  output s
);

  wire and_1_out, and_2_out, not_1_out, not_2_out, not_3_out, or_1_out;

  not not_1 (not_1_out, x);
  not not_2 (not_2_out, x);
  or or_1 (or_1_out, not_2_out, not_3_out);
  not not_3 (not_3_out, y);
  and and_1 (and_1_out, w, z, not_1_out);
  and and_2 (and_2_out, w, z, or_1_out);
  or or_2 (s, and_1_out, and_2_out);
endmodule

module questao_3c (
  input  x,
  input  y,
  input  w,
  input  z,
  output s
);

  wire and_1_out, and_2_out, and_3_out, and_4_out, and_5_out, and_6_out, and_7_out, not_1_out, not_2_out,
       not_3_out, not_4_out, not_5_out, not_6_out, not_7_out, not_8_out, not_9_out, not_10_out, not_11_out,
       not_12_out;

  not not_1 (not_1_out, x);
  not not_2 (not_2_out, w);
  and and_1 (and_1_out, not_1_out, not_2_out, not_3_out);
  not not_3 (not_3_out, y);
  not not_4 (not_4_out, x);
  not not_5 (not_5_out, z);
  and and_2 (and_2_out, not_4_out, not_5_out, not_6_out);
  not not_6 (not_6_out, y);
  not not_7 (not_7_out, x);
  and and_3 (and_3_out, not_7_out, w, y);
  not not_8 (not_8_out, y);
  and and_4 (and_4_out, not_8_out, w, not_9_out);
  not not_9 (not_9_out, z);
  and and_5 (and_5_out, x, w, z);
  and and_6 (and_6_out, x, w, not_10_out);
  not not_10 (not_10_out, y);
  and and_7 (and_7_out, w, not_11_out, not_12_out);
  not not_11 (not_11_out, z);
  not not_12 (not_12_out, y);
  or or_1 (s, and_1_out, and_2_out, and_3_out, and_4_out, and_5_out, and_6_out, and_7_out);
endmodule

module questao_3d (
  input  x,
  input  y,
  input  w,
  input  z,
  output s
);

  wire and_1_out, and_2_out, and_3_out, and_4_out, and_5_out, not_1_out, not_2_out, not_3_out, not_4_out,
       not_5_out, not_6_out, not_7_out;

  not not_1 (not_1_out, x);
  and and_1 (and_1_out, not_1_out, not_2_out, y);
  not not_2 (not_2_out, z);
  not not_3 (not_3_out, y);
  and and_2 (and_2_out, not_3_out, w, not_4_out);
  not not_4 (not_4_out, z);
  not not_5 (not_5_out, x);
  and and_3 (and_3_out, not_5_out, w, y);
  not not_6 (not_6_out, w);
  and and_4 (and_4_out, x, not_6_out, z);
  and and_5 (and_5_out, y, w, not_7_out);
  not not_7 (not_7_out, z);
  or or_1 (s, and_1_out, and_2_out, and_3_out, and_4_out, and_5_out);
endmodule

module questao_3e (
  input  x,
  input  y,
  input  w,
  input  z,
  output s
);

  wire and_1_out, and_2_out, and_3_out, and_4_out, and_5_out, not_1_out, not_2_out, not_3_out, not_4_out,
       not_5_out, not_6_out, not_7_out, not_8_out, or_1_out;

  not not_1 (not_1_out, y);
  not not_2 (not_2_out, w);
  and and_1 (and_1_out, not_2_out, z);
  not not_3 (not_3_out, x);
  or or_1 (or_1_out, not_1_out, z, and_1_out);
  not not_4 (not_4_out, w);
  not not_5 (not_5_out, y);
  not not_6 (not_6_out, w);
  not not_7 (not_7_out, z);
  not not_8 (not_8_out, w);
  and and_2 (and_2_out, not_3_out, or_1_out);
  and and_3 (and_3_out, x, not_4_out, y);
  and and_4 (and_4_out, not_5_out, not_6_out, not_7_out);
  and and_5 (and_5_out, y, not_8_out, z);
  or or_2 (s, and_2_out, and_3_out, and_4_out, and_5_out);
endmodule
