// Logisim project questao_04.circ as structural Verilog: 5 circuits, main circuit questao_4a
module questao_4a (
  input  X,
  input  Z,
  input  Y,
  output s
);

  wire not_1_out, not_2_out, not_3_out, or_1_out, or_2_out;

  not not_1 (not_1_out, Y);
  not not_2 (not_2_out, Z);
  not not_3 (not_3_out, Z);
  or or_1 (or_1_out, not_1_out, not_2_out);
  or or_2 (or_2_out, X, not_3_out);
  and and_1 (s, or_1_out, or_2_out);
endmodule

module questao_4b (
  input  Z,
  input  W,
  output s
);

  wire not_1_out, not_2_out;

  not not_1 (not_1_out, Z);
  not not_2 (not_2_out, W);
  or or_1 (s, 1'b1, Z, not_1_out, not_2_out);
endmodule

module questao_4c (
  input  X,
  input  Y,
  output s
);

  wire not_1_out, not_2_out;

  not not_1 (not_1_out, X);
  not not_2 (not_2_out, Y);
  and and_1 (s, not_1_out, not_2_out);
endmodule

module questao_4d (
  input  X,
  input  Y,
  input  W,
  input  Z,
  output s
);

  wire not_1_out, not_2_out, not_3_out, not_4_out, not_5_out, or_1_out, or_2_out;

  not not_1 (not_1_out, Z);
  or or_1 (or_1_out, not_1_out, not_2_out);
  not not_2 (not_2_out, Y);
  not not_3 (not_3_out, X);
  or or_2 (or_2_out, not_3_out, not_4_out, not_5_out);
  not not_4 (not_4_out, W);
  not not_5 (not_5_out, Y);
  and and_1 (s, X, or_1_out, or_2_out);
endmodule

module questao_4e (
  input  X,
  input  Y,
  input  W,
  input  Z,
  output s
);

  wire not_1_out, not_2_out, not_3_out, not_4_out, not_5_out, or_1_out, or_2_out, or_3_out;

  or or_1 (or_1_out, X, not_1_out);
  not not_1 (not_1_out, Y);
  not not_2 (not_2_out, X);
  not not_3 (not_3_out, W);
  or or_2 (or_2_out, not_2_out, not_3_out, not_4_out);
  not not_4 (not_4_out, Y);
  not not_5 (not_5_out, Z);
  or or_3 (or_3_out, not_5_out, W);
  and and_1 (s, or_1_out, or_2_out, or_3_out);
endmodule
