// Logisim project questao_05.circ as structural Verilog: 1 circuit, main circuit questao_05
module questao_05 (
  input  x,
  input  y,
  input  z,
  output s
);

  wire not_1_out, not_2_out, or_1_out, or_2_out;

  not not_1 (not_1_out, y);
  not not_2 (not_2_out, z);
  or or_1 (or_1_out, x, z);
  or or_2 (or_2_out, not_1_out, not_2_out);
  and and_1 (s, or_1_out, or_2_out);
endmodule
