// Logisim project questao_06.circ as structural Verilog: 1 circuit, main circuit questao_06
module questao_06 (
  input  x,
  input  y,
  input  w,
  input  z,
  output s
);

  wire and_1_out, and_2_out, not_1_out, not_2_out, not_3_out, not_4_out;

  not not_1 (not_1_out, x);
  not not_2 (not_2_out, y);
  not not_3 (not_3_out, w);
  not not_4 (not_4_out, z);
  and and_1 (and_1_out, not_1_out, y);
  or or_1 (s, and_1_out, and_2_out);
  and and_2 (and_2_out, x, not_2_out, not_3_out, not_4_out);
endmodule
