// Logisim project Guia_0801.circ as structural Verilog: 2 circuits, main circuit main
module main (
  input  in_1,
  input  in_2,
  input  in_3,
  input  in_4,
  input  in_5,
  input  in_6,
  input  in_7,
  input  in_8,
  input  in_9,
  input  in_10,
  output out_11,
  output out_12,
  output out_13,
  output out_14,
  output out_15
);

  wire adicionar_2_out_5, adicionar_3_out_5, adicionar_4_out_5, adicionar_5_out_5;

  Adicionar adicionar_1 (.x(in_1), .y(in_2), .vai_um(adicionar_2_out_5), .s(out_11));  // open: out_5
  Adicionar adicionar_2 (.x(in_3), .y(in_4), .vai_um(adicionar_3_out_5), .s(out_12), .out_5(adicionar_2_out_5));
  Adicionar adicionar_3 (.x(in_5), .y(in_6), .vai_um(adicionar_4_out_5), .s(out_13), .out_5(adicionar_3_out_5));
  Adicionar adicionar_4 (.x(in_7), .y(in_8), .vai_um(adicionar_5_out_5), .s(out_14), .out_5(adicionar_4_out_5));
  Adicionar adicionar_5 (.x(in_9), .y(in_10), .vai_um(1'b0), .s(out_15), .out_5(adicionar_5_out_5));
endmodule

module Adicionar (
  input  x,
  input  y,
  input  vai_um,
  output s,
  output out_5
);

  wire and_1_out, and_2_out, xor_1_out;

  xor xor_1 (xor_1_out, x, y);
  and and_1 (and_1_out, x, y);
  xor xor_2 (s, vai_um, xor_1_out);
  and and_2 (and_2_out, xor_1_out, vai_um);
  or or_1 (out_5, and_2_out, and_1_out);
endmodule
