// Logisim project Guia_0802.circ as structural Verilog: 3 circuits, main circuit main
module main (
  input  A,
  input  B,
  input  in_3,
  input  in_4,
  input  in_5,
  input  in_6,
  input  in_7,
  input  in_8,
  input  in_9,
  input  in_10,
  input  in_11,
  input  in_12,
  output out_13,
  output out_14,
  output out_15,
  output out_16,
  output out_17,
  output out_18
);

  wire full_subtractor_2_out_5, full_subtractor_3_out_5, full_subtractor_4_out_5, full_subtractor_5_out_5;

  full_subtractor full_subtractor_1 (.vem_um(full_subtractor_2_out_5), .a(A), .b(B), .diff(out_13));  // open: out_5
  full_subtractor full_subtractor_2 (
    .vem_um(full_subtractor_3_out_5), .a(in_3), .b(in_4), .diff(out_14), .out_5(full_subtractor_2_out_5));
  full_subtractor full_subtractor_3 (
    .vem_um(full_subtractor_4_out_5), .a(in_5), .b(in_6), .diff(out_15), .out_5(full_subtractor_3_out_5));
  full_subtractor full_subtractor_4 (
    .vem_um(full_subtractor_5_out_5), .a(in_7), .b(in_8), .diff(out_16), .out_5(full_subtractor_4_out_5));
  full_subtractor full_subtractor_5 (
    .vem_um(out_18), .a(in_9), .b(in_10), .diff(out_17), .out_5(full_subtractor_5_out_5));
  full_subtractor full_subtractor_6 (.vem_um(1'b0), .a(in_11), .b(in_12), .diff(out_18), .out_5(out_18));
endmodule

module half_subtractor (
  input  a,
  input  b,
  output out_3,
  output out_4
);

  wire not_1_out;

  not not_1 (not_1_out, a);
  xor xor_1 (out_3, a, b);
  and and_1 (out_4, b, not_1_out);
endmodule

module full_subtractor (
  input  vem_um,
  input  a,
  input  b,
  output diff,
  output out_5
);

  wire half_subtractor_1_out_4, half_subtractor_2_out_3, half_subtractor_2_out_4;

  half_subtractor half_subtractor_1 (
    .a(vem_um), .b(half_subtractor_2_out_3), .out_3(diff), .out_4(half_subtractor_1_out_4));
  half_subtractor half_subtractor_2 (.a(a), .b(b), .out_3(half_subtractor_2_out_3), .out_4(half_subtractor_2_out_4));
  or or_1 (out_5, half_subtractor_1_out_4, half_subtractor_2_out_4);
endmodule
