// Logisim project Guia_0803.circ as structural Verilog: 2 circuits, main circuit main
module main (
  input  A,
  input  B,
  input  in_3,
  input  in_4,
  input  in_5,
  input  in_6,
  input  in_7,
  input  in_8,
  input  in_9,
  input  in_10,
  input  in_11,
  input  in_12,
  output out_13
);

  wire comparador_1_igual, comparador_2_igual, comparador_3_igual, comparador_4_igual, comparador_5_igual,
       comparador_6_igual;

  comparador comparador_1 (.a(A), .b(B), .Igual(comparador_1_igual));  // open: a_b, a_b_2
  comparador comparador_2 (.a(in_3), .b(in_4), .Igual(comparador_2_igual));  // open: a_b, a_b_2
  comparador comparador_3 (.a(in_5), .b(in_6), .Igual(comparador_3_igual));  // open: a_b, a_b_2
  and and_1 (out_13, comparador_1_igual, comparador_2_igual, comparador_3_igual, comparador_4_igual, comparador_5_igual, comparador_6_igual);
  comparador comparador_4 (.a(in_7), .b(in_8), .Igual(comparador_4_igual));  // open: a_b, a_b_2
  comparador comparador_5 (.a(in_9), .b(in_10), .Igual(comparador_5_igual));  // open: a_b, a_b_2
  comparador comparador_6 (.a(in_11), .b(in_12), .Igual(comparador_6_igual));  // open: a_b, a_b_2
endmodule

module comparador (
  input  a,
  input  b,
  output a_b,
  output Igual,
  output a_b_2
);

  wire not_1_out, not_2_out;

  not not_1 (not_1_out, a);
  not not_2 (not_2_out, b);
  and and_1 (a_b, not_1_out, b);
  xnor xnor_1 (Igual, a, b);
  and and_2 (a_b_2, not_2_out, a);
endmodule
