// Logisim project Guia_0805.circ as structural Verilog: 3 circuits, main circuit main
module main (
  input  in_1,
  input  in_2,
  input  in_3,
  input  in_4,
  input  in_5,
  output out_6,
  output out_7,
  output out_8,
  output out_9,
  output out_10
);

  wire adicionar_2_vem_um, adicionar_3_vem_um, adicionar_4_vem_um, adicionar_5_vem_um, complemento_1_out_6,
       complemento_1_out_7, complemento_1_out_8, complemento_1_out_9, complemento_1_out_10;

  adicionar adicionar_1 (.x(complemento_1_out_6), .y(1'b0), .vai_um(adicionar_2_vem_um), .s(out_6));  // open: vem_um
  Complemento complemento_1 (
    .in_1(in_1), .in_2(in_2), .in_3(in_3), .in_4(in_4), .in_5(in_5), .out_6(complemento_1_out_6),
    .out_7(complemento_1_out_7), .out_8(complemento_1_out_8), .out_9(complemento_1_out_9),
    .out_10(complemento_1_out_10));
  adicionar adicionar_2 (
    .x(complemento_1_out_7), .y(1'b0), .vai_um(adicionar_3_vem_um), .s(out_7), .vem_um(adicionar_2_vem_um));
  adicionar adicionar_3 (
    .x(complemento_1_out_8), .y(1'b0), .vai_um(adicionar_4_vem_um), .s(out_8), .vem_um(adicionar_3_vem_um));
  adicionar adicionar_4 (
    .x(complemento_1_out_9), .y(1'b0), .vai_um(adicionar_5_vem_um), .s(out_9), .vem_um(adicionar_4_vem_um));
  adicionar adicionar_5 (.x(complemento_1_out_10), .y(1'b0), .vai_um(1'b1), .s(out_10), .vem_um(adicionar_5_vem_um));
endmodule

module Complemento (
  input  in_1,
  input  in_2,
  input  in_3,
  input  in_4,
  input  in_5,
  output out_6,
  output out_7,
  output out_8,
  output out_9,
  output out_10
);

  not not_1 (out_7, in_2);
  not not_2 (out_6, in_1);
  not not_3 (out_8, in_3);
  not not_4 (out_9, in_4);
  not not_5 (out_10, in_5);
endmodule

module adicionar (
  input  x,
  input  y,
  input  vai_um,
  output s,
  output vem_um
);

  wire and_1_out, and_2_out, xor_1_out;

  xor xor_1 (xor_1_out, x, y);
  and and_1 (and_1_out, x, y);
  xor xor_2 (s, vai_um, xor_1_out);
  and and_2 (and_2_out, xor_1_out, vai_um);
  or or_1 (vem_um, and_2_out, and_1_out);
endmodule
