// Logisim project Guia_1202.circ as structural Verilog: 3 circuits, main circuit 1202
module _1202 (
  input  ADDR,
  input  R_W,
  input  CLK,
  input  CLEAR,
  input  x1,
  input  x2,
  input  x2_2,
  input  x2_3,
  input  x2_4,
  input  x2_5,
  input  x2_6,
  input  x2_7,
  output [7:0] out_13
);

  RAM_1x4 ram_1x4_1 (
    .ADDR(ADDR), .R_W(R_W), .CLK(CLK), .x1_2(out_13[7]), .x2_2(R_W), .x3_2(out_13[5]), .x4_2(out_13[4]),
    .x1(CLEAR), .x2(CLEAR), .x3(CLEAR), .x4(CLEAR));  // open: CLEAR
  RAM_1x4 ram_1x4_2 (
    .ADDR(ADDR), .R_W(R_W), .CLK(CLK), .x1_2(out_13[3]), .x2_2(out_13[2]), .x3_2(out_13[1]),
    .x4_2(out_13[0]), .x1(CLEAR), .x2(x2_4), .x3(x2_5), .x4(x2_6));  // open: CLEAR

  assign out_13[6] = R_W;
  assign x1 = CLEAR;
  assign x2 = CLEAR;
  assign x2_2 = CLEAR;
endmodule

module MEMORY (
  input  ADDR,
  input  R_W,
  input  CLK,
  input  IN,
  input  CLEAR,
  output out_6
);

  wire and_1_out, j_k_ff_1_q, not_1_out;

  and and_1 (and_1_out, ADDR, R_W, CLK);
  not not_1 (not_1_out, IN);
  J_K_Flip_Flop j_k_ff_1 (.J(IN), .clk(and_1_out), .K(not_1_out), .Q(j_k_ff_1_q), .reset(CLEAR));  // open: Qn, preset
  and and_2 (out_6, ADDR, j_k_ff_1_q);
endmodule

module RAM_1x4 (
  input  ADDR,
  input  R_W,
  input  CLK,
  input  CLEAR,
  input  x1,
  input  x2,
  input  x3,
  input  x4,
  output x1_2,
  output x2_2,
  output x3_2,
  output x4_2
);

  MEMORY memory_1 (.R_W(ADDR), .CLK(R_W), .IN(CLK), .CLEAR(x1), .out_6(x1_2));  // open: ADDR
  MEMORY memory_2 (.R_W(ADDR), .CLK(R_W), .IN(CLK), .CLEAR(x2), .out_6(x2_2));  // open: ADDR
  MEMORY memory_3 (.R_W(ADDR), .CLK(R_W), .IN(CLK), .CLEAR(x3), .out_6(x3_2));  // open: ADDR
  MEMORY memory_4 (.R_W(ADDR), .CLK(R_W), .IN(CLK), .CLEAR(x4), .out_6(x4_2));  // open: ADDR
endmodule
