// Logisim project questao_1b.circ as structural Verilog: 1 circuit, main circuit 1b
module _1b (
  input  a,
  input  b,
  input  c,
  input  d,
  output \saída 
);

  wire not_1_out, not_2_out, not_3_out, not_4_out, or_1_out, or_2_out, or_3_out, or_4_out, or_5_out,
       or_6_out, or_7_out, or_8_out, or_9_out;

  not not_1 (not_1_out, a);
  not not_2 (not_2_out, b);
  not not_3 (not_3_out, c);
  not not_4 (not_4_out, d);
  or or_1 (or_1_out, a, not_2_out, c, d);
  or or_2 (or_2_out, a, not_2_out, not_3_out, d);
  or or_3 (or_3_out, a, not_2_out, not_3_out, not_4_out);
  or or_4 (or_4_out, not_1_out, b, c, not_4_out);
  or or_5 (or_5_out, not_1_out, b, not_3_out, d);
  or or_6 (or_6_out, not_1_out, b, not_3_out, not_4_out);
  or or_7 (or_7_out, not_1_out, not_2_out, c, d);
  or or_8 (or_8_out, not_1_out, not_2_out, not_3_out, d);
  or or_9 (or_9_out, not_1_out, not_2_out, not_3_out, not_4_out);
  and and_1 (\saída , or_1_out, or_2_out, or_3_out, or_4_out, or_5_out, or_6_out, or_7_out, or_8_out, or_9_out);
endmodule
