// Logisim project questao_1c.circ as structural Verilog: 1 circuit, main circuit 1c
module _1c (
  input  a,
  input  b,
  input  c,
  input  d,
  output \saída 
);

  wire and_1_out, and_2_out, and_3_out, not_1_out, not_2_out, not_3_out, not_4_out;

  not not_1 (not_1_out, b);
  not not_2 (not_2_out, a);
  not not_3 (not_3_out, c);
  not not_4 (not_4_out, d);
  and and_1 (and_1_out, not_2_out, not_1_out);
  and and_2 (and_2_out, b, not_3_out, d);
  and and_3 (and_3_out, not_1_out, not_3_out, not_4_out);
  or or_1 (\saída , and_1_out, and_2_out, and_3_out);
endmodule
