// Logisim project questao_1d.circ as structural Verilog: 1 circuit, main circuit 1d
module _1d (
  input  a,
  input  b,
  input  c,
  input  d,
  output \sáida 
);

  wire not_1_out, not_2_out, not_3_out, not_4_out, or_1_out, or_2_out, or_3_out, or_4_out;

  not not_1 (not_1_out, a);
  not not_2 (not_2_out, b);
  not not_3 (not_3_out, c);
  not not_4 (not_4_out, d);
  or or_1 (or_1_out, not_2_out, not_3_out);
  or or_2 (or_2_out, not_1_out, b, not_3_out);
  or or_3 (or_3_out, not_1_out, b, not_4_out);
  or or_4 (or_4_out, not_2_out, c, d);
  and and_1 (\sáida , or_1_out, or_2_out, or_3_out, or_4_out);
endmodule
