// Logisim project questao_1f.circ as structural Verilog: 1 circuit, main circuit 1f
module _1f (
  input  a,
  input  b,
  input  c,
  input  d,
  output \saída 
);

  wire nor_1_out, nor_2_out, nor_3_out, nor_4_out, nor_5_out, nor_6_out, nor_7_out, nor_8_out, nor_9_out,
       nor_10_out, nor_11_out, nor_12_out, not_1_out, not_2_out, not_3_out, not_4_out;

  not not_1 (not_1_out, b);
  not not_2 (not_2_out, a);
  not not_3 (not_3_out, d);
  not not_4 (not_4_out, c);
  nor nor_1 (nor_1_out, not_1_out, not_4_out);
  nor nor_2 (nor_2_out, not_2_out, b, not_4_out);
  nor nor_3 (nor_3_out, not_2_out, b, not_3_out);
  nor nor_4 (nor_4_out, not_1_out, c, d);
  nor nor_5 (nor_5_out, nor_1_out, nor_1_out);
  nor nor_6 (nor_6_out, nor_2_out, nor_2_out);
  nor nor_7 (nor_7_out, nor_3_out, nor_3_out);
  nor nor_8 (nor_8_out, nor_4_out, nor_4_out);
  nor nor_9 (nor_9_out, nor_5_out, nor_5_out);
  nor nor_10 (nor_10_out, nor_6_out, nor_6_out);
  nor nor_11 (nor_11_out, nor_7_out, nor_7_out);
  nor nor_12 (nor_12_out, nor_8_out, nor_8_out);
  nor nor_13 (\saída , nor_9_out, nor_10_out, nor_11_out, nor_12_out);
endmodule
