// Logisim project questao_2a.circ as structural Verilog: 1 circuit, main circuit main
module main (
  input  a,
  input  b,
  output \saída 
);

  wire and_1_out, not_1_out, not_2_out, or_1_out;

  not not_1 (not_1_out, b);
  and and_1 (and_1_out, not_1_out, a);
  or or_1 (or_1_out, a, b);
  not not_2 (not_2_out, and_1_out);
  or or_2 (\saída , not_2_out, or_1_out);
endmodule
