// Logisim project questao_3a.circ as structural Verilog: 1 circuit, main circuit 3a
module _3a (
  input  a,
  input  b,
  input  c,
  input  d,
  output \saída 
);

  wire nand_1_out, nand_2_out;

  nand nand_1 (nand_1_out, a, c);
  nand nand_2 (nand_2_out, b, d);
  nand nand_3 (\saída , nand_1_out, nand_2_out);
endmodule
