// Logisim project questao_3b.circ as structural Verilog: 1 circuit, main circuit 3b
module _3b (
  input  a,
  input  b,
  input  c,
  output \saída 
);

  wire multiplexer_1_out, multiplexer_2_out, not_1_out, not_2_out, not_3_out;

  not not_1 (not_1_out, a);
  not not_2 (not_2_out, b);
  Multiplexer #(.enable("false")) multiplexer_1 (.in0(b), .in1(c), .out(multiplexer_1_out), .sel(a));
  Multiplexer #(.enable("false")) multiplexer_2 (.in0(not_1_out), .in1(not_2_out), .out(multiplexer_2_out), .sel(c));
  not not_3 (not_3_out, c);
  Multiplexer #(.enable("false")) multiplexer_3 (
    .in0(multiplexer_1_out), .in1(multiplexer_2_out), .out(\saída ), .sel(not_3_out));
endmodule
