// Logisim project questao_04a.circ as structural Verilog: 1 circuit, main circuit questao_04
module questao_04a (
  input  a,
  input  b,
  input  c,
  input  click,
  output s
);

  wire and_1_out, and_2_out, not_1_out, not_2_out, or_1_out;

  not not_1 (not_1_out, b);
  not not_2 (not_2_out, c);
  and and_1 (and_1_out, c, not_1_out);
  or or_1 (or_1_out, and_1_out, and_2_out);
  and and_2 (and_2_out, a, not_2_out);
  D_Flip_Flop d_ff_1 (.clk(click), .D(or_1_out), .Q(s));  // open: Qn, preset, reset
endmodule
