// Logisim project questao_04b.circ as structural Verilog: 1 circuit, main circuit questao_04b
module questao_04b (
  input  a,
  input  b,
  input  c,
  input  click,
  output s
);

  wire and_1_out, and_2_out, not_1_out, not_2_out;

  not not_1 (not_1_out, a);
  not not_2 (not_2_out, b);
  and and_1 (and_1_out, not_1_out, b, c);
  and and_2 (and_2_out, a, not_2_out, c);
  J_K_Flip_Flop j_k_ff_1 (.J(and_1_out), .clk(click), .K(and_2_out), .Q(s));  // open: Qn, preset, reset
endmodule
