// Logisim project questao_04d.circ as structural Verilog: 1 circuit, main circuit questao_04d
module questao_04d (
  input  a,
  input  b,
  input  c,
  input  click,
  output s
);

  wire and_1_out, and_2_out, not_1_out, not_2_out;

  not not_1 (not_1_out, a);
  not not_2 (not_2_out, b);
  and and_1 (and_1_out, not_1_out, not_2_out, c);
  and and_2 (and_2_out, a, b, c);
  S_R_Flip_Flop s_r_ff_1 (.S(and_1_out), .clk(click), .R(and_2_out), .Q(s));  // open: Qn, preset, reset
endmodule
