// Logisim project questao_04e.circ as structural Verilog: 1 circuit, main circuit questao_04e
module questao_04e (
  input  a,
  input  b,
  input  c,
  input  click,
  output s
);

  wire and_1_out, and_2_out, not_1_out, not_2_out, or_1_out;

  not not_1 (not_1_out, b);
  not not_2 (not_2_out, a);
  and and_1 (and_1_out, not_2_out, not_1_out, c);
  and and_2 (and_2_out, a, b, c);
  or or_1 (or_1_out, and_1_out, and_2_out);
  T_Flip_Flop t_ff_1 (.clk(click), .T(or_1_out), .Q(s));  // open: Qn, preset, reset
endmodule
