// Logisim project questao_05a.circ as structural Verilog: 1 circuit, main circuit questao_05a
module questao_05a (
  input  in_1,
  input  in_2,
  input  in_3,
  output a,
  output b,
  output c,
  output d
);

  D_Flip_Flop #(.Pre_Clr_Positions("LEGACY"), .enable("true"), .NewFFLayout("false")) d_ff_1 (
    .clk(in_1), .D(in_2), .Q(a), .reset(in_3));  // open: Qn, preset, en
  D_Flip_Flop #(.Pre_Clr_Positions("LEGACY"), .enable("true"), .NewFFLayout("false")) d_ff_2 (
    .clk(in_1), .D(a), .Q(b), .reset(in_3));  // open: Qn, preset, en
  D_Flip_Flop #(.Pre_Clr_Positions("LEGACY"), .enable("true"), .NewFFLayout("false")) d_ff_3 (
    .clk(in_1), .D(b), .Q(c), .reset(in_3));  // open: Qn, preset, en
  D_Flip_Flop #(.Pre_Clr_Positions("LEGACY"), .enable("true"), .NewFFLayout("false")) d_ff_4 (
    .clk(in_1), .D(c), .Q(d), .reset(in_3));  // open: Qn, preset, en
endmodule
