// Logisim project questao_05b.circ as structural Verilog: 1 circuit, main circuit questao_05b
module questao_05b (
  input  click,
  input  ld,
  input  clear,
  output a,
  output b,
  output c,
  output d
);

  D_Flip_Flop #(.Pre_Clr_Positions("LEGACY"), .enable("true"), .NewFFLayout("false")) d_ff_1 (
    .clk(click), .D(b), .Q(a), .reset(clear));  // open: Qn, preset, en
  D_Flip_Flop #(.Pre_Clr_Positions("LEGACY"), .enable("true"), .NewFFLayout("false")) d_ff_2 (
    .clk(click), .D(c), .Q(b), .reset(clear));  // open: Qn, preset, en
  D_Flip_Flop #(.Pre_Clr_Positions("LEGACY"), .enable("true"), .NewFFLayout("false")) d_ff_3 (
    .clk(click), .D(d), .Q(c), .reset(clear));  // open: Qn, preset, en
  D_Flip_Flop #(.Pre_Clr_Positions("LEGACY"), .enable("true"), .NewFFLayout("false")) d_ff_4 (
    .clk(click), .D(ld), .Q(d), .reset(clear));  // open: Qn, preset, en
endmodule
