// Logisim project questao_05c.circ as structural Verilog: 1 circuit, main circuit questao_05c
module questao_05c (
  input  click,
  input  clear,
  output a,
  output b,
  output c,
  output d
);

  wire xor_1_out;

  D_Flip_Flop #(.Pre_Clr_Positions("LEGACY"), .enable("true"), .NewFFLayout("false")) d_ff_1 (
    .clk(click), .D(xor_1_out), .Q(a), .reset(clear));  // open: Qn, preset, en
  xor xor_1 (xor_1_out, 1'b1, d);
  D_Flip_Flop #(.Pre_Clr_Positions("LEGACY"), .enable("true"), .NewFFLayout("false")) d_ff_2 (
    .clk(click), .D(a), .Q(b), .reset(clear));  // open: Qn, preset, en
  D_Flip_Flop #(.Pre_Clr_Positions("LEGACY"), .enable("true"), .NewFFLayout("false")) d_ff_3 (
    .clk(click), .D(b), .Q(c), .reset(clear));  // open: Qn, preset, en
  D_Flip_Flop #(.Pre_Clr_Positions("LEGACY"), .enable("true"), .NewFFLayout("false")) d_ff_4 (
    .clk(click), .D(c), .Q(d), .reset(clear));  // open: Qn, preset, en
endmodule
