// Logisim project questao_05d.circ as structural Verilog: 1 circuit, main circuit questao_05d
module questao_05d (
  input  click,
  input  clear,
  output a,
  output b,
  output c,
  output d
);

  wire nand_1_out;

  D_Flip_Flop #(.Pre_Clr_Positions("LEGACY"), .enable("true"), .NewFFLayout("false")) d_ff_1 (
    .clk(click), .D(nand_1_out), .Q(a), .reset(clear));  // open: Qn, preset, en
  nand nand_1 (nand_1_out, 1'b0, d);
  D_Flip_Flop #(.Pre_Clr_Positions("LEGACY"), .enable("true"), .NewFFLayout("false")) d_ff_2 (
    .clk(click), .D(a), .Q(b), .reset(clear));  // open: Qn, preset, en
  D_Flip_Flop #(.Pre_Clr_Positions("LEGACY"), .enable("true"), .NewFFLayout("false")) d_ff_3 (
    .clk(click), .D(b), .Q(c), .reset(clear));  // open: Qn, preset, en
  D_Flip_Flop #(.Pre_Clr_Positions("LEGACY"), .enable("true"), .NewFFLayout("false")) d_ff_4 (
    .clk(click), .D(c), .Q(d), .reset(clear));  // open: Qn, preset, en
endmodule
