// Logisim project atividade_01.circ as structural Verilog: 5 circuits, main circuit soma_4bits
module soma_4bits (
  input  constante,
  input  a0,
  input  b0,
  input  a1,
  input  b1,
  input  a2,
  input  b2,
  input  a3,
  input  b3,
  output s0,
  output s1,
  output s2,
  output s3,
  output co,
  output overflow
);

  wire soma_completa_1_con, soma_completa_2_con, soma_completa_3_con;

  soma_completa soma_completa_1 (.an(a0), .bn(b0), .cin(constante), .con(soma_completa_1_con), .sn(s0));
  soma_completa soma_completa_2 (.an(a1), .bn(b1), .cin(soma_completa_1_con), .con(soma_completa_2_con), .sn(s1));
  soma_completa soma_completa_3 (.an(a2), .bn(b2), .cin(soma_completa_2_con), .con(soma_completa_3_con), .sn(s2));
  soma_completa soma_completa_4 (.an(a3), .bn(b3), .cin(soma_completa_3_con), .con(co), .sn(s3));
  xor xor_1 (overflow, soma_completa_3_con, co);
endmodule

module meia_soma (
  input  x0,
  input  y0,
  output s0,
  output co0
);

  and and_1 (co0, x0, y0);
  xor xor_1 (s0, x0, y0);
endmodule

module soma_completa (
  input  cin,
  input  an,
  input  bn,
  output sn,
  output con
);

  wire meia_soma_1_co0, meia_soma_1_s0, meia_soma_2_co0;

  meia_soma meia_soma_1 (.x0(an), .y0(bn), .co0(meia_soma_1_co0), .s0(meia_soma_1_s0));
  meia_soma meia_soma_2 (.x0(cin), .y0(meia_soma_1_s0), .co0(meia_soma_2_co0), .s0(sn));
  or or_1 (con, meia_soma_2_co0, meia_soma_1_co0);
endmodule

module main (
  input  A0,
  input  B0,
  input  Constante,
  input  A1,
  input  B1,
  input  A2,
  input  B2,
  input  A3,
  input  B3,
  output S0,
  output S1,
  output S2,
  output Co,
  output S3,
  output out_15
);

  wire decodificador_1_a, decodificador_1_b, decodificador_1_c, decodificador_1_d, decodificador_1_e,
       decodificador_1_f, decodificador_1_g, decodificador_2_a, decodificador_2_b, decodificador_2_c,
       decodificador_2_d, decodificador_2_e, decodificador_2_f, decodificador_2_g, decodificador_3_a,
       decodificador_3_b, decodificador_3_c, decodificador_3_d, decodificador_3_e, decodificador_3_f,
       decodificador_3_g;

  decodificador decodificador_1 (
    .E3(A3), .E2(A2), .E1(A1), .E0(A0), .a(decodificador_1_a), .b(decodificador_1_b), .c(decodificador_1_c),
    .d(decodificador_1_d), .e(decodificador_1_e), .f(decodificador_1_f), .g(decodificador_1_g));
  soma_4bits soma_4bits_1 (
    .a0(A0), .b0(B0), .a1(A1), .b1(B1), .a2(A2), .b2(B2), .a3(A3), .b3(B3), .constante(Constante), .co(Co),
    .s0(S0), .s1(S1), .s2(S2), .s3(S3), .overflow(out_15));
  decodificador decodificador_2 (
    .E3(B3), .E2(B2), .E1(B1), .E0(B0), .a(decodificador_2_a), .b(decodificador_2_b), .c(decodificador_2_c),
    .d(decodificador_2_d), .e(decodificador_2_e), .f(decodificador_2_f), .g(decodificador_2_g));
  _7_Segment_Display u_7_segment_display_1 (
    .g(decodificador_2_g), .f(decodificador_2_f), .a(decodificador_2_a), .b(decodificador_2_b),
    .e(decodificador_2_e), .d(decodificador_2_d), .c(decodificador_2_c));  // open: dp
  _7_Segment_Display u_7_segment_display_2 (
    .g(decodificador_1_g), .f(decodificador_1_f), .a(decodificador_1_a), .b(decodificador_1_b),
    .e(decodificador_1_e), .d(decodificador_1_d), .c(decodificador_1_c));  // open: dp
  decodificador decodificador_3 (
    .E3(S3), .E2(S2), .E1(S1), .E0(S0), .a(decodificador_3_a), .b(decodificador_3_b), .c(decodificador_3_c),
    .d(decodificador_3_d), .e(decodificador_3_e), .f(decodificador_3_f), .g(decodificador_3_g));
  _7_Segment_Display u_7_segment_display_3 (
    .g(decodificador_3_g), .f(decodificador_3_f), .a(decodificador_3_a), .b(decodificador_3_b),
    .e(decodificador_3_e), .d(decodificador_3_d), .c(decodificador_3_c));  // open: dp
endmodule

module decodificador (
  input  E3,
  input  E2,
  input  E1,
  input  E0,
  output a,
  output b,
  output c,
  output d,
  output e,
  output f,
  output g
);

  wire nand_1_out, nand_2_out, nand_3_out, nand_4_out, nand_5_out, nand_6_out, nand_7_out, nand_8_out,
       nand_9_out, nand_10_out, nand_11_out, nand_12_out, nand_13_out, nand_14_out, nand_15_out, nand_16_out,
       nand_17_out, nand_18_out, nand_19_out, nand_20_out, nand_21_out, nand_22_out, nand_23_out,
       nand_24_out, nand_25_out, nand_26_out, nand_27_out, nand_28_out, nand_29_out, nand_30_out,
       nand_31_out, nand_32_out, nand_33_out, nand_34_out, nand_35_out, nand_36_out, nand_37_out,
       nand_38_out, nand_39_out, nand_40_out, nand_41_out, nand_42_out, nand_43_out, nand_44_out,
       nand_45_out, nand_46_out, nand_47_out, nand_48_out, nand_49_out, nand_50_out, nand_51_out,
       nand_52_out, nand_53_out, nand_54_out, nand_55_out, nand_56_out, nand_57_out, nand_58_out,
       nand_59_out, nand_60_out, nand_61_out, nand_62_out, nand_63_out, nand_64_out, nand_65_out,
       nand_66_out, nand_67_out, nand_68_out, nand_69_out, nand_70_out, nand_71_out, nand_72_out,
       nand_73_out, nand_74_out, nand_75_out, nand_76_out, nand_77_out, nand_78_out;

  nand nand_1 (nand_1_out, E2, E2);
  nand nand_2 (nand_2_out, E0, E0);
  nand nand_3 (nand_3_out, E3, E3);
  nand nand_4 (nand_4_out, E3, E3);
  nand nand_5 (nand_5_out, E2, E2);
  nand nand_6 (nand_6_out, E1, E1);
  nand nand_7 (nand_7_out, E0, E0);
  nand nand_8 (nand_8_out, E3, E3);
  nand nand_9 (nand_9_out, E2, E2);
  nand nand_10 (nand_10_out, E3, E3);
  nand nand_11 (nand_11_out, E1, E1);
  nand nand_12 (nand_12_out, E0, E0);
  nand nand_13 (nand_13_out, E2, E2);
  nand nand_14 (nand_14_out, E0, E0);
  nand nand_15 (nand_15_out, E3, E3);
  nand nand_16 (nand_16_out, E1, E1);
  nand nand_17 (nand_17_out, E3, E3);
  nand nand_18 (nand_18_out, E1, E1);
  nand nand_19 (nand_19_out, E3, E3);
  nand nand_20 (nand_20_out, E1, E1);
  nand nand_21 (nand_21_out, E3, E3);
  nand nand_22 (nand_22_out, E2, E2);
  nand nand_23 (nand_23_out, E3, E3);
  nand nand_24 (nand_24_out, E2, E2);
  nand nand_25 (nand_25_out, E0, E0);
  nand nand_26 (nand_26_out, E2, E2);
  nand nand_27 (nand_27_out, E1, E1);
  nand nand_28 (nand_28_out, E0, E0);
  nand nand_29 (nand_29_out, E3, E3);
  nand nand_30 (nand_30_out, E0, E0);
  nand nand_31 (nand_31_out, E2, E2);
  nand nand_32 (nand_32_out, E1, E1);
  nand nand_33 (nand_33_out, E2, E2);
  nand nand_34 (nand_34_out, E0, E0);
  nand nand_35 (nand_35_out, E0, E0);
  nand nand_36 (nand_36_out, E2, E2);
  nand nand_37 (nand_37_out, E1, E1);
  nand nand_38 (nand_38_out, E1, E1);
  nand nand_39 (nand_39_out, E0, E0);
  nand nand_40 (nand_40_out, E3, E3);
  nand nand_41 (nand_41_out, E2, E2);
  nand nand_42 (nand_42_out, E2, E2);
  nand nand_43 (nand_43_out, E1, E1);
  nand nand_44 (nand_44_out, E0, E0);
  nand nand_45 (nand_45_out, nand_1_out, nand_2_out);
  nand nand_46 (nand_46_out, nand_3_out, E1);
  nand nand_47 (nand_47_out, nand_4_out, E2, E0);
  nand nand_48 (nand_48_out, E2, E1);
  nand nand_49 (nand_49_out, E3, nand_5_out, nand_6_out);
  nand nand_50 (nand_50_out, E3, nand_7_out);
  nand nand_51 (nand_51_out, nand_8_out, nand_9_out);
  nand nand_52 (nand_52_out, nand_10_out, nand_11_out, nand_12_out);
  nand nand_53 (nand_53_out, nand_13_out, nand_14_out);
  nand nand_54 (nand_54_out, nand_15_out, E1, E0);
  nand nand_55 (nand_55_out, E3, nand_16_out, E0);
  nand nand_56 (nand_56_out, nand_17_out, nand_18_out);
  nand nand_57 (nand_57_out, nand_19_out, E0);
  nand nand_58 (nand_58_out, nand_20_out, E0);
  nand nand_59 (nand_59_out, nand_21_out, E2);
  nand nand_60 (nand_60_out, E3, nand_22_out);
  nand nand_61 (nand_61_out, nand_23_out, nand_24_out, nand_25_out);
  nand nand_62 (nand_62_out, nand_26_out, nand_27_out, nand_28_out);
  nand nand_63 (nand_63_out, nand_29_out, E1, nand_30_out);
  nand nand_64 (nand_64_out, nand_31_out, E1, E0);
  nand nand_65 (nand_65_out, E2, nand_32_out, E0);
  nand nand_66 (nand_66_out, E3, E2);
  nand nand_67 (nand_67_out, nand_33_out, nand_34_out);
  nand nand_68 (nand_68_out, E1, nand_35_out);
  nand nand_69 (nand_69_out, E3, nand_36_out, E1);
  nand nand_70 (nand_70_out, E3, E2, nand_37_out);
  nand nand_71 (nand_71_out, nand_38_out, nand_39_out);
  nand nand_72 (nand_72_out, nand_40_out, E2);
  nand nand_73 (nand_73_out, E3, nand_41_out);
  nand nand_74 (nand_74_out, E3, E1);
  nand nand_75 (nand_75_out, nand_42_out, E1);
  nand nand_76 (nand_76_out, E2, nand_43_out);
  nand nand_77 (nand_77_out, E2, nand_44_out);
  nand nand_78 (nand_78_out, E3, E3);
  nand nand_79 (a, nand_45_out, nand_46_out, nand_47_out, nand_48_out, nand_49_out, nand_50_out);
  nand nand_80 (b, nand_51_out, nand_52_out, nand_53_out, nand_54_out, nand_55_out);
  nand nand_81 (c, nand_56_out, nand_57_out, nand_58_out, nand_59_out, nand_60_out);
  nand nand_82 (d, nand_61_out, nand_62_out, nand_63_out, nand_64_out, nand_65_out, nand_66_out);
  nand nand_83 (e, nand_67_out, nand_68_out, nand_69_out, nand_70_out);
  nand nand_84 (f, nand_71_out, nand_72_out, nand_73_out, nand_74_out);
  nand nand_85 (g, nand_75_out, nand_76_out, nand_77_out, nand_78_out);
endmodule
