// Logisim project atividade_02.circ as structural Verilog: 6 circuits, main circuit ULA_2bit
module ULA_2bit (
  input  BInvert,
  input  CarryIn,
  input  Op1,
  input  Op0,
  input  A,
  input  B,
  output Result,
  output CarryOut
);

  wire and_1_out, MUX_2x1_result, not_1_out, not_2_out, or_1_out, somador_sum;

  not not_1 (not_1_out, B);
  MUX_2x1 MUX_2x1 (.A(B), .B(not_1_out), .OP(BInvert), .Result(MUX_2x1_result));
  and and_1 (and_1_out, A, MUX_2x1_result);
  or or_1 (or_1_out, A, MUX_2x1_result);
  not not_2 (not_2_out, A);
  somador somador (.a(A), .b(MUX_2x1_result), .CarryIn(CarryIn), .Sum(somador_sum), .Overflow(CarryOut));
  MUX_4x2 MUX_4x2 (.M(and_1_out), .N(or_1_out), .O(not_2_out), .P(somador_sum), .Op1(Op1), .Op0(Op0), .Result(Result));
endmodule

module MUX_2x1 (
  input  OP,
  input  A,
  input  B,
  output Result
);

  wire and_1_out, and_2_out, not_1_out;

  not not_1 (not_1_out, OP);
  and and_1 (and_1_out, A, not_1_out);
  and and_2 (and_2_out, B, OP);
  or or_1 (Result, and_1_out, and_2_out);
endmodule

module MUX_4x2 (
  input  Op1,
  input  Op0,
  input  M,
  input  N,
  input  O,
  input  P,
  output Result
);

  wire and_1_out, and_2_out, and_3_out, and_4_out, not_1_out, not_2_out, not_3_out, not_4_out;

  not not_1 (not_1_out, Op1);
  not not_2 (not_2_out, Op0);
  not not_3 (not_3_out, Op1);
  not not_4 (not_4_out, Op0);
  and and_1 (and_1_out, M, not_1_out, not_2_out);
  and and_2 (and_2_out, N, not_3_out, Op0);
  and and_3 (and_3_out, O, Op1, not_4_out);
  and and_4 (and_4_out, P, Op1, Op0);
  or or_1 (Result, and_1_out, and_2_out, and_3_out, and_4_out);
endmodule

module ULA_4bits (
  input  Op1,
  input  Op0,
  input  BInvert,
  input  A0,
  input  B0,
  input  A1,
  input  B1,
  input  A2,
  input  B2,
  input  A3,
  input  B3,
  output S0,
  output S1,
  output S2,
  output S3,
  output Carryout
);

  wire ula_2bit_1_carryout, ula_2bit_2_carryout, ula_2bit_3_carryout;

  ULA_2bit ula_2bit_1 (
    .A(A0), .B(B0), .BInvert(BInvert), .CarryIn(BInvert), .Op1(Op1), .Op0(Op0),
    .CarryOut(ula_2bit_1_carryout), .Result(S0));
  ULA_2bit ula_2bit_2 (
    .A(A1), .B(B1), .BInvert(BInvert), .CarryIn(ula_2bit_1_carryout), .Op1(Op1), .Op0(Op0),
    .CarryOut(ula_2bit_2_carryout), .Result(S1));
  ULA_2bit ula_2bit_3 (
    .A(A2), .B(B2), .BInvert(BInvert), .CarryIn(ula_2bit_2_carryout), .Op1(Op1), .Op0(Op0),
    .CarryOut(ula_2bit_3_carryout), .Result(S2));
  ULA_2bit ula_2bit_4 (
    .A(A3), .B(B3), .BInvert(BInvert), .CarryIn(ula_2bit_3_carryout), .Op1(Op1), .Op0(Op0),
    .CarryOut(Carryout), .Result(S3));
endmodule

module somador (
  input  CarryIn,
  input  a,
  input  b,
  output Sum,
  output Overflow
);

  wire and_1_out, and_2_out, xor_1_out;

  xor xor_1 (xor_1_out, a, b);
  and and_1 (and_1_out, a, b);
  xor xor_2 (Sum, xor_1_out, CarryIn);
  and and_2 (and_2_out, CarryIn, xor_1_out);
  or or_1 (Overflow, and_2_out, and_1_out);
endmodule

module Main (
  input  [3:0] A,
  input  [3:0] B,
  input  [3:0] Op,
  output [3:0] out_4
);

  wire [3:0] and_1_out, and_2_out, and_3_out, nand_1_out, nor_1_out, not_1_out, not_2_out, not_3_out,
       not_4_out, not_5_out, or_1_out, or_2_out, or_3_out, xnor_1_out, xor_1_out;

  assign not_1_out = ~B;  // NOT_Gate not_1, 4 bits wide
  assign not_2_out = ~4'b0000;  // NOT_Gate not_2, 4 bits wide
  assign not_3_out = ~B;  // NOT_Gate not_3, 4 bits wide
  assign not_4_out = ~A;  // NOT_Gate not_4, 4 bits wide
  assign nor_1_out = ~(A | B);  // NOR_Gate nor_1, 4 bits wide
  assign nand_1_out = ~(A & B);  // NAND_Gate nand_1, 4 bits wide
  assign xor_1_out = A ^ B;  // XOR_Gate xor_1, 4 bits wide
  assign and_1_out = A & not_1_out;  // AND_Gate and_1, 4 bits wide
  assign or_1_out = not_2_out | B;  // OR_Gate or_1, 4 bits wide
  assign xnor_1_out = ~(4'b0000 ^ B);  // XNOR_Gate xnor_1, 4 bits wide
  assign and_2_out = 4'b0000 & B;  // AND_Gate and_2, 4 bits wide
  assign or_2_out = 4'b0000 | not_3_out;  // OR_Gate or_2, 4 bits wide
  assign or_3_out = A | B;  // OR_Gate or_3, 4 bits wide
  assign and_3_out = not_4_out & B;  // AND_Gate and_3, 4 bits wide
  assign not_5_out = ~B;  // NOT_Gate not_5, 4 bits wide
  Multiplexer #(.select(4), .width(4), .enable("false")) multiplexer_1 (
    .in0(not_4_out), .in1(nor_1_out), .in2(and_3_out), .in3(4'b0000), .in4(nand_1_out), .in5(not_5_out),
    .in6(xor_1_out), .in7(and_1_out), .in8(or_1_out), .in9(xnor_1_out), .in10(B), .in11(and_2_out),
    .in12(4'b1111), .in13(or_2_out), .in14(or_3_out), .in15(A), .out(out_4), .sel(Op));
endmodule
